# Fritzing sketch XIAOGPT (saved by Fritzing 1.0.4)
breadboards: 1

parts:
  XIAO_ESP32S1 = XIAO ESP32S3 [package="DIP (Dual Inline) [THT]"]
  Part1 = Adafruit MAX98357A I2S 3W Class D Amplifier [part_number="Adafruit #3006"]
  Part2 = INMP441
  SP1 = SPEAKER [package=pcb_mount_speaker]

nets:
  N1: XIAO_ESP32S1.D4, Part2.WS
  N2: XIAO_ESP32S1.D5, Part2.SCK
  N3: XIAO_ESP32S1.D7, Part2.SD
  N4: XIAO_ESP32S1.D8, Part1.LRCLK
  N5: XIAO_ESP32S1.D9, Part1.BCLK
  N6: XIAO_ESP32S1.D10, Part1.DIN
  3V3: XIAO_ESP32S1.3V3, Part1.VIN, Part2.VDD
  GND: XIAO_ESP32S1.GND, Part1.GND, Part1.GAIN, Part2.L/R, Part2.GND
  N7: Part1.VO-, SP1.+
  N8: Part1.VO+, SP1.-

custom parts:
  XIAO ESP32S3: Seeed Studio XIAO ESP32S3 leverages 240MHz Xtensa 32-bit LX7 dual-core processor, supporting both WiFi and BLE 5.0 wireless connectivities, a 2.4GHz Rod antenna, allows for deep sleep mode with power consumption as low as 14μA while supporting lithium battery charging management. Ideal for the Internet of Things, Smart Homes, Wireless wearable devices, Robotics, etc.
  Adafruit MAX98357A I2S 3W Class D Amplifier: Listen to this good news - we now have an all in one digital audio amp breakout board that works incredibly well with the Raspberry Pi! If you're looking for an easy and low cost way to get you digital sound files bumpin' then the MAX08357 I2S Amp Breakout is for you. It takes standard I2S digital audio input and, not only decodes it into analog, but also amplifies it directly into a speaker.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
  INMP441: This is a simple breakout board for the INMP441 I2S MEMS microphone.
